// Logisim project Home Automator Additional.circ as structural Verilog: 1 circuit, main circuit main
module main (
  input  A3,
  input  A2,
  input  A1,
  input  A0,
  input  B3,
  input  B2,
  input  B1,
  input  B0,
  input  C3,
  input  C2,
  input  C1,
  input  C0,
  output L1,
  output L2,
  output F1,
  output F2,
  output Wifi_Transmitter,
  output Wifi_Transmitter_2,
  output Wifi_Transmitter_3
);

  wire All_Off_Reset_out, and_1_out, clock_1_out, counter_2_carry, decoder_1_out0, decoder_1_out1,
       decoder_1_out2, decoder_1_out3, decoder_1_out4, decoder_1_out5, decoder_1_out6, decoder_2_out0,
       decoder_2_out1, decoder_2_out2, decoder_2_out3, decoder_2_out4, decoder_2_out5, decoder_2_out6,
       decoder_2_out7, Hold_to_debug_out, nor_1_out, not_1_out, or_1_out, or_2_out, or_3_out, or_6_out,
       priority_encoder_1_out;
  wire [1:0] counter_2_q;
  wire [2:0] counter_1_q, shift_register_1_out, shift_register_1_q0, shift_register_1_q1,
       shift_register_1_q2, shift_register_1_q3;
  wire [3:0] shift_register_2_q3;
  wire [3:2] register_1_q;

  Clock clock_1 (.out(clock_1_out));
  Decoder #(.select(3), .enable("false")) decoder_1 (
    .out0(decoder_1_out0), .out1(decoder_1_out1), .out2(decoder_1_out2), .out3(decoder_1_out3),
    .out4(decoder_1_out4), .out5(decoder_1_out5), .out6(decoder_1_out6), .sel(counter_1_q));  // open: out7
  Counter #(.width(3), .max('h7)) counter_1 (
    .Q(counter_1_q), .clk(clock_1_out), .clr(or_1_out));  // open: load, D, count, carry
  or or_1 (or_1_out, decoder_1_out6, Hold_to_debug_out, or_3_out, Wifi_Transmitter_3);
  Button Hold_to_debug (.out(Hold_to_debug_out));
  Shift_Register #(.width(3), .length(4)) shift_register_1 (
    .shift(or_2_out), .in(shift_register_1_out), .clk(clock_1_out), .out(shift_register_1_out),
    .load(decoder_1_out0), .clr(Wifi_Transmitter_3), .d0({A3, A2, A1}), .q0(shift_register_1_q0),
    .d1({B3, A0, B2}), .q1(shift_register_1_q1), .d2({C3, B1, B0}), .q2(shift_register_1_q2),
    .d3({C2, C1, C0}), .q3(shift_register_1_q3));
  or or_2 (or_2_out, decoder_1_out1, decoder_1_out2, decoder_1_out3, decoder_1_out4);
  // Probe on shift_register_1_q1
  // Probe on shift_register_1_q0
  // Probe on shift_register_1_q2
  // Probe on shift_register_1_q3
  Decoder #(.select(3), .enable("false")) decoder_2 (
    .out0(decoder_2_out0), .out1(decoder_2_out1), .out2(decoder_2_out2), .out3(decoder_2_out3),
    .out4(decoder_2_out4), .out5(decoder_2_out5), .out6(decoder_2_out6), .out7(decoder_2_out7),
    .sel(shift_register_1_out));
  nor nor_1 (nor_1_out, A2, A1, B3, B2, B0, C3, C1, C0);
  and and_1 (and_1_out, nor_1_out, A3, A0, B1, C2);
  not not_1 (not_1_out, and_1_out);
  Priority_Encoder #(.select(1)) priority_encoder_1 (
    .in0(decoder_2_out1), .in1(decoder_2_out2), .out(priority_encoder_1_out));  // open: gs, en_out, en_in
  or or_3 (or_3_out, decoder_2_out0, decoder_2_out3, decoder_2_out4, decoder_2_out5, decoder_2_out6, decoder_2_out7);
  LED Invalid (.in(or_3_out));
  Counter #(.width(2), .max('h3)) counter_2 (
    .count(and_1_out), .Q(counter_2_q), .carry(counter_2_carry), .clk(clock_1_out), .clr(not_1_out));  // open: load, D
  or or_4 (L2, counter_2_q[1], register_1_q[2]);
  or or_5 (L1, counter_2_q[0], register_1_q[3]);
  Shift_Register #(.length(4)) shift_register_2 (
    .shift(or_2_out), .in(priority_encoder_1_out), .clk(clock_1_out), .load(counter_2_carry),
    .clr(Wifi_Transmitter_3), .d0(1'b0), .q0(shift_register_2_q3[3]), .d1(1'b0), .q1(shift_register_2_q3[2]),
    .d2(F1), .q2(shift_register_2_q3[1]), .d3(F2), .q3(shift_register_2_q3[0]));  // open: out
  or or_6 (or_6_out, counter_2_carry, decoder_1_out5);
  Button All_Off_Reset (.out(All_Off_Reset_out));
  Register #(.width(4)) register_1 (
    .D(shift_register_2_q3), .en(or_6_out), .Q({register_1_q, F1, F2}), .clk(clock_1_out),
    .clr(Wifi_Transmitter_3));
  D_Flip_Flop d_ff_1 (.clk(clock_1_out), .D(All_Off_Reset_out), .Q(Wifi_Transmitter_3));  // open: Qn, preset, en, reset
  Counter #(.width(4), .max('hf)) counter_3 (
    .count(F1), .carry(Wifi_Transmitter_2), .clk(clock_1_out));  // open: load, D, Q, clr
  Counter #(.width(4), .max('hf)) counter_4 (
    .count(F2), .carry(Wifi_Transmitter), .clk(clock_1_out));  // open: load, D, Q, clr

  // Notes on the sheet:
  //   Clock
  //   Debug Mode
  //   12 Bit BCD Input
  //                  HOME AUTOMATOR
  //   Party Mode
  //   Output
  //   Kill Switch/ power OFF
  //                           Power consumption counter
  //   for fans 1,2
endmodule
