// Logisim project Home Automator.circ as structural Verilog: 1 circuit, main circuit main
module main (
  input  A3,
  input  A2,
  input  A1,
  input  A0,
  input  B3,
  input  B2,
  input  B1,
  input  B0,
  input  C3,
  input  C2,
  input  C1,
  input  C0,
  output L1,
  output L2,
  output F1,
  output F2
);

  wire clock_1_out, decoder_1_out0, decoder_1_out1, decoder_1_out2, decoder_1_out3, decoder_1_out4,
       decoder_1_out5, decoder_1_out6, decoder_2_out0, decoder_2_out1, decoder_2_out2, decoder_2_out3,
       decoder_2_out4, decoder_2_out5, decoder_2_out6, decoder_2_out7, G1_out, or_1_out, or_2_out,
       priority_encoder_1_out;
  wire [2:0] counter_1_q, shift_register_1_out;
  wire [3:0] shift_register_2_q3;

  Clock clock_1 (.out(clock_1_out));
  Decoder #(.select(3), .enable("false")) decoder_1 (
    .out0(decoder_1_out0), .out1(decoder_1_out1), .out2(decoder_1_out2), .out3(decoder_1_out3),
    .out4(decoder_1_out4), .out5(decoder_1_out5), .out6(decoder_1_out6), .sel(counter_1_q));  // open: out7
  Counter #(.width(3), .max('h7)) counter_1 (
    .Q(counter_1_q), .clk(clock_1_out), .clr(G1_out));  // open: load, D, count, carry
  or G1 (G1_out, decoder_1_out6, or_2_out);
  or or_1 (or_1_out, decoder_1_out1, decoder_1_out2, decoder_1_out3, decoder_1_out4);
  Shift_Register #(.width(3), .length(4)) shift_register_1 (
    .shift(or_1_out), .in(shift_register_1_out), .clk(clock_1_out), .out(shift_register_1_out),
    .load(decoder_1_out0), .d0({A3, A2, A1}), .d1({B3, A0, B2}), .d2({C3, B1, B0}), .d3({C2, C1, C0}));  // open: clr, q0, q1, q2, q3
  Decoder #(.select(3), .enable("false")) decoder_2 (
    .out0(decoder_2_out0), .out1(decoder_2_out1), .out2(decoder_2_out2), .out3(decoder_2_out3),
    .out4(decoder_2_out4), .out5(decoder_2_out5), .out6(decoder_2_out6), .out7(decoder_2_out7),
    .sel(shift_register_1_out));
  or or_2 (or_2_out, decoder_2_out0, decoder_2_out3, decoder_2_out4, decoder_2_out5, decoder_2_out6, decoder_2_out7);
  Priority_Encoder #(.select(1)) priority_encoder_1 (
    .in0(decoder_2_out1), .in1(decoder_2_out2), .out(priority_encoder_1_out));  // open: gs, en_out, en_in
  Shift_Register #(.length(4)) shift_register_2 (
    .shift(or_1_out), .in(priority_encoder_1_out), .clk(clock_1_out), .q0(shift_register_2_q3[3]),
    .q1(shift_register_2_q3[2]), .q2(shift_register_2_q3[1]), .q3(shift_register_2_q3[0]));  // open: out, load, clr, d0, d1, d2, d3
  LED led_1 (.in(or_2_out));
  Register #(.width(4)) register_1 (
    .D(shift_register_2_q3), .en(decoder_1_out5), .Q({L1, L2, F1, F2}), .clk(clock_1_out));  // open: clr

  // Notes on the sheet:
  //   Counter 1
  //   Decoder 1
  //   Clock
  //   G2
  //   Register 1
  //   12 Bit BCD input
  //   Decoder 2
  //          HOME AUTOMATOR
  //   Priority 1
  //   G3
  //    Invalid
  //   Register 2
  //   Output
  //   Register 3
  //   L1- Light1
  //            L2-Light2
  //          F1- Fan1
  //   F2- Fan 2     
  //   Devices ON at 1 and OFF at 0
  //                                         Output may change at every 6 clock cycles
  //   depending on the input
endmodule
