// Logisim project markI.circ as structural Verilog: 1 circuit, main circuit main
module main (
  input  A3,
  input  A2,
  input  A1,
  input  A0,
  input  B3,
  input  B2,
  input  B1,
  input  B0,
  input  C3,
  input  C2,
  input  C1,
  input  C0,
  output F1,
  output F2,
  output L1,
  output L2
);

  wire and_1_out, and_2_out, and_3_out, and_4_out, and_5_out, and_6_out, and_7_out, and_8_out, and_9_out,
       clock_1_out, not_1_out, not_2_out, not_3_out, not_4_out, or_1_out, or_2_out, or_3_out, or_4_out,
       or_5_out, or_6_out, xor_1_out, xor_2_out, xor_3_out;
  wire [1:0] priority_encoder_1_out;

  and and_1 (and_1_out, F1, or_1_out);
  or or_1 (or_1_out, A2, A1, A0);
  not not_1 (not_1_out, or_1_out);
  and and_2 (and_2_out, F2, or_2_out);
  or or_2 (or_2_out, B2, B1, B0);
  not not_2 (not_2_out, or_2_out);
  Priority_Encoder #(.select(2)) priority_encoder_1 (
    .in0(C0), .in1(C1), .in2(C2), .in3(C3), .out(priority_encoder_1_out), .en_in(1'b1));  // open: gs, en_out
  not not_3 (not_3_out, not_4_out);
  ExactlyOne xor_1 (.out(xor_1_out), .in0(C3), .in1(C2), .in2(C1), .in3(C0));
  and and_3 (and_3_out, C2, C1, C0);
  and and_4 (and_4_out, A3, not_1_out);
  and and_5 (and_5_out, B3, not_2_out);
  and and_6 (and_6_out, priority_encoder_1_out[0], not_3_out);
  and and_7 (and_7_out, L1, not_4_out);
  not not_4 (not_4_out, xor_2_out);
  xor xor_2 (xor_2_out, xor_3_out, and_3_out);
  xor xor_3 (xor_3_out, xor_1_out, and_3_out);
  or or_3 (or_3_out, and_1_out, and_4_out);
  or or_4 (or_4_out, and_2_out, and_5_out);
  or or_5 (or_5_out, and_6_out, and_7_out);
  and and_8 (and_8_out, priority_encoder_1_out[1], not_3_out);
  and and_9 (and_9_out, not_4_out, L2);
  Clock clock_1 (.out(clock_1_out));
  D_Flip_Flop d_ff_1 (.clk(clock_1_out), .D(or_3_out), .Q(F1), .en(1'b1));  // open: Qn, preset, reset
  D_Flip_Flop d_ff_2 (.clk(clock_1_out), .D(or_4_out), .Q(F2), .en(1'b1));  // open: Qn, preset, reset
  D_Flip_Flop d_ff_3 (.clk(clock_1_out), .D(or_5_out), .Q(L1), .en(1'b1));  // open: Qn, preset, reset
  D_Flip_Flop d_ff_4 (.clk(clock_1_out), .D(or_6_out), .Q(L2), .en(1'b1));  // open: Qn, preset, reset
  or or_6 (or_6_out, and_8_out, and_9_out);
endmodule
