// Logisim project markII.circ as structural Verilog: 1 circuit, main circuit main
module main (
  input  Fan_1_On_Off,
  input  A2,
  input  A1,
  input  A0,
  input  Fan_2_On_Off,
  input  B2,
  input  B1,
  input  B0,
  input  Both_On,
  input  Light_2_On,
  input  Light_1_On,
  input  Both_Off,
  output F1,
  output F2,
  output L1,
  output L2
);

  wire and_1_out, and_2_out, and_3_out, and_4_out, and_5_out, and_6_out, and_7_out, and_8_out, and_9_out,
       clock_1_out, nor_1_out, not_1_out, not_2_out, not_3_out, not_4_out, or_1_out, or_2_out, xor_1_out,
       xor_2_out, xor_3_out;
  wire [1:0] priority_encoder_1_out;
  wire [3:0] or_3_out;

  and and_1 (and_1_out, F1, or_1_out);
  not not_1 (not_1_out, or_1_out);
  or or_1 (or_1_out, A2, A1, A0);
  and and_2 (and_2_out, F2, or_2_out);
  or or_2 (or_2_out, B2, B1, B0);
  not not_2 (not_2_out, or_2_out);
  Priority_Encoder #(.select(2)) priority_encoder_1 (
    .in0(Both_Off), .in1(Light_1_On), .in2(Light_2_On), .in3(Both_On), .out(priority_encoder_1_out),
    .en_in(1'b1));  // open: gs, en_out
  not not_3 (not_3_out, not_4_out);
  ExactlyOne xor_1 (.out(xor_1_out), .in0(Both_On), .in1(Light_2_On), .in2(Light_1_On), .in3(Both_Off));
  and and_3 (and_3_out, Light_2_On, Light_1_On, Both_Off);
  and and_4 (and_4_out, Fan_1_On_Off, not_1_out);
  and and_5 (and_5_out, Fan_2_On_Off, not_2_out);
  and and_6 (and_6_out, priority_encoder_1_out[0], not_3_out);
  and and_7 (and_7_out, L1, not_4_out);
  not not_4 (not_4_out, xor_2_out);
  xor xor_2 (xor_2_out, xor_3_out, and_3_out);
  xor xor_3 (xor_3_out, xor_1_out, and_3_out);
  or or_3 (or_3_out[0], and_1_out, and_4_out);
  or or_4 (or_3_out[1], and_2_out, and_5_out);
  or or_5 (or_3_out[2], and_6_out, and_7_out);
  and and_8 (and_8_out, priority_encoder_1_out[1], not_3_out);
  and and_9 (and_9_out, not_4_out, L2);
  nor nor_1 (nor_1_out, or_1_out, not_4_out, or_2_out);
  or or_6 (or_3_out[3], and_8_out, and_9_out);
  Register #(.width(4)) register_1 (
    .D(or_3_out), .en(nor_1_out), .Q({L2, L1, F2, F1}), .clk(clock_1_out));  // open: clr
  Clock clock_1 (.out(clock_1_out));
endmodule
