// Logisim project markIII.circ as structural Verilog: 1 circuit, main circuit main
module main (
  input  Fan_1_On_Off,
  input  A2,
  input  A1,
  input  A0,
  input  Fan_2_On_Off,
  input  A2_2,
  input  A1_2,
  input  A0_2,
  input  Both_On,
  input  Light_2_On,
  input  Clear,
  input  Light_1_On,
  input  Both_Off,
  output F1,
  output F2,
  output L1,
  output L2
);

  wire and_1_out, Clock_out, nand_1_out, nand_2_out, nand_3_out, nand_4_out, nand_5_out, nand_6_out,
       nand_7_out, nand_8_out, nand_9_out, nand_10_out, nand_11_out, nand_12_out, nand_13_out, nand_14_out,
       nand_15_out, nand_16_out, nand_17_out, nand_18_out, nand_19_out, xnor_1_out, xor_1_out, xor_2_out;
  wire [1:0] priority_encoder_1_out;

  nand nand_1 (nand_1_out, A2, A2);
  nand nand_2 (nand_2_out, A1, A1);
  nand nand_3 (nand_3_out, A0, A0);
  nand nand_4 (nand_4_out, A2_2, A2_2);
  nand nand_5 (nand_5_out, A1_2, A1_2);
  nand nand_6 (nand_6_out, A0_2, A0_2);
  ExactlyOne xor_1 (.out(xor_1_out), .in0(Both_Off), .in1(Light_1_On), .in2(Light_2_On), .in3(Both_On));
  and and_1 (and_1_out, Both_Off, Light_1_On, Light_2_On);
  nand nand_7 (nand_7_out, nand_1_out, nand_2_out);
  nand nand_8 (nand_8_out, nand_4_out, nand_5_out);
  xor xor_2 (xor_2_out, xor_1_out, and_1_out);
  nand nand_9 (nand_9_out, nand_7_out, nand_7_out);
  nand nand_10 (nand_10_out, nand_9_out, nand_3_out);
  nand nand_11 (nand_11_out, nand_8_out, nand_8_out);
  nand nand_12 (nand_12_out, nand_11_out, nand_6_out);
  Priority_Encoder #(.select(2), .disabled(0)) priority_encoder_1 (
    .in0(Both_Off), .in1(Light_1_On), .in2(Light_2_On), .in3(Both_On), .out(priority_encoder_1_out),
    .en_in(1'b1));  // open: gs, en_out
  xnor xnor_1 (xnor_1_out, xor_2_out, and_1_out);
  nand nand_13 (nand_13_out, nand_10_out, nand_10_out);
  nand nand_14 (nand_14_out, nand_12_out, nand_12_out);
  nand nand_15 (nand_15_out, xnor_1_out, xnor_1_out);
  nand nand_16 (nand_16_out, nand_13_out, nand_14_out);
  nand nand_17 (nand_17_out, nand_16_out, nand_16_out);
  nand nand_18 (nand_18_out, nand_17_out, nand_15_out);
  nand nand_19 (nand_19_out, nand_18_out, nand_18_out);
  Register #(.width(4)) register_1 (
    .D({priority_encoder_1_out, Fan_2_On_Off, Fan_1_On_Off}), .en(nand_19_out), .Q({L2, L1, F2, F1}),
    .clk(Clock_out), .clr(Clear));
  Clock Clock (.out(Clock_out));
  LED Valid (.in(nand_19_out));
endmodule
