// Logisim project markIV.circ as structural Verilog: 1 circuit, main circuit main
module main (
  input  Fan_1_On_Off,
  input  A2,
  input  A1,
  input  A0,
  input  Fan_2_On_Off,
  input  A2_2,
  input  A1_2,
  input  A0_2,
  input  Clear,
  input  Both_On,
  input  Light_2_On,
  input  Light_1_On,
  input  Both_Off,
  output F1,
  output F2,
  output L1,
  output L2
);

  wire adder_1_cout, adder_1_out, adder_2_cout, adder_2_out, Clock_out, nand_1_out, nand_2_out, nand_3_out,
       nand_4_out, nand_5_out, nand_6_out, nand_7_out, nand_8_out, nand_9_out, nand_10_out, nand_11_out,
       nand_12_out, nand_13_out, nand_14_out, nand_15_out, nand_16_out, nand_17_out, nand_18_out,
       nand_19_out, nand_20_out, nand_21_out, nand_22_out, nand_23_out, nand_24_out, nand_25_out;
  wire [1:0] priority_encoder_1_out;

  nand nand_1 (nand_1_out, A2, A2);
  nand nand_2 (nand_2_out, A1, A1);
  nand nand_3 (nand_3_out, A0, A0);
  nand nand_4 (nand_4_out, A2_2, A2_2);
  nand nand_5 (nand_5_out, A1_2, A1_2);
  nand nand_6 (nand_6_out, A0_2, A0_2);
  nand nand_7 (nand_7_out, nand_1_out, nand_2_out);
  nand nand_8 (nand_8_out, nand_4_out, nand_5_out);
  nand nand_9 (nand_9_out, Both_On, Both_On);
  Adder #(.width(1)) adder_1 (.a(nand_9_out), .b(nand_10_out), .out(adder_1_out), .cout(adder_1_cout));  // open: cin
  nand nand_10 (nand_10_out, Light_2_On, Light_2_On);
  nand nand_11 (nand_11_out, Light_1_On, Light_1_On);
  Adder #(.width(1)) adder_2 (.a(nand_11_out), .b(nand_12_out), .out(adder_2_out), .cout(adder_2_cout));  // open: cin
  nand nand_12 (nand_12_out, Both_Off, Both_Off);
  nand nand_13 (nand_13_out, nand_7_out, nand_7_out);
  nand nand_14 (nand_14_out, nand_13_out, nand_3_out);
  nand nand_15 (nand_15_out, nand_8_out, nand_8_out);
  nand nand_16 (nand_16_out, nand_15_out, nand_6_out);
  Priority_Encoder #(.select(2), .disabled(0)) priority_encoder_1 (
    .in0(Both_Off), .in1(Light_1_On), .in2(Light_2_On), .in3(Both_On), .out(priority_encoder_1_out),
    .en_in(1'b1));  // open: gs, en_out
  nand nand_17 (nand_17_out, adder_1_out, adder_2_cout);
  nand nand_18 (nand_18_out, adder_1_cout, adder_2_out);
  nand nand_19 (nand_19_out, nand_14_out, nand_14_out);
  nand nand_20 (nand_20_out, nand_16_out, nand_16_out);
  nand nand_21 (nand_21_out, nand_17_out, nand_18_out);
  nand nand_22 (nand_22_out, nand_19_out, nand_20_out);
  nand nand_23 (nand_23_out, nand_22_out, nand_22_out);
  nand nand_24 (nand_24_out, nand_25_out, nand_25_out);
  nand nand_25 (nand_25_out, nand_23_out, nand_21_out);
  Register #(.width(4)) register_1 (
    .D({priority_encoder_1_out, Fan_2_On_Off, Fan_1_On_Off}), .en(nand_24_out), .Q({L2, L1, F2, F1}),
    .clk(Clock_out), .clr(Clear));
  Clock Clock (.out(Clock_out));
  LED Valid (.in(nand_24_out));
endmodule
