// Logisim project markV.circ as structural Verilog: 1 circuit, main circuit main
module main (
  input  Fan_1_On_Off,
  input  A2,
  input  A1,
  input  A0,
  input  Fan_2_On_Off,
  input  A2_2,
  input  A1_2,
  input  A0_2,
  input  Clear,
  input  Both_On,
  input  Light_2_On,
  input  Light_1_On,
  input  Both_Off,
  output F1,
  output F2,
  output L1,
  output L2
);

  wire adder_1_cout, adder_1_out, adder_2_cout, adder_2_out, Clock_out, nand_1_out, nand_2_out, nand_3_out,
       nand_4_out, nand_5_out, nand_6_out, nand_7_out, priority_encoder_1_gs, priority_encoder_2_gs,
       priority_encoder_3_gs;
  wire [1:0] priority_encoder_1_out, priority_encoder_4_out, priority_encoder_5_out;

  // Probe on priority_encoder_1_out
  Priority_Encoder #(.select(2)) priority_encoder_1 (
    .in0(A2), .in1(A1), .in2(A0), .in3(1'b0), .out(priority_encoder_1_out), .gs(priority_encoder_1_gs));  // open: en_out, en_in
  Priority_Encoder #(.select(2)) priority_encoder_2 (
    .in0(A2_2), .in1(A1_2), .in2(A0_2), .in3(1'b0), .gs(priority_encoder_2_gs));  // open: out, en_out, en_in
  nand nand_1 (nand_1_out, Both_On, Both_On);
  Adder #(.width(1)) adder_1 (.a(nand_1_out), .b(nand_2_out), .out(adder_1_out), .cout(adder_1_cout));  // open: cin
  nand nand_2 (nand_2_out, Light_2_On, Light_2_On);
  nand nand_3 (nand_3_out, Light_1_On, Light_1_On);
  Adder #(.width(1)) adder_2 (.a(nand_3_out), .b(nand_4_out), .out(adder_2_out), .cout(adder_2_cout));  // open: cin
  nand nand_4 (nand_4_out, Both_Off, Both_Off);
  Priority_Encoder #(.select(2)) priority_encoder_3 (
    .in0(1'b0), .in1(1'b0), .in2(priority_encoder_1_gs), .in3(priority_encoder_2_gs),
    .gs(priority_encoder_3_gs));  // open: out, en_out, en_in
  Priority_Encoder #(.select(2), .disabled(0)) priority_encoder_4 (
    .in0(Both_Off), .in1(Light_1_On), .in2(Light_2_On), .in3(Both_On), .out(priority_encoder_4_out),
    .en_in(1'b1));  // open: gs, en_out
  nand nand_5 (nand_5_out, adder_1_out, adder_2_cout);
  nand nand_6 (nand_6_out, adder_1_cout, adder_2_out);
  Priority_Encoder #(.select(2)) priority_encoder_5 (
    .in0(1'b1), .in1(nand_7_out), .in2(priority_encoder_3_gs), .in3(1'b0), .out(priority_encoder_5_out),
    .en_in(1'b1));  // open: gs, en_out
  nand nand_7 (nand_7_out, nand_5_out, nand_6_out);
  Register #(.width(4)) register_1 (
    .D({priority_encoder_4_out, Fan_2_On_Off, Fan_1_On_Off}), .en(priority_encoder_5_out[0]),
    .Q({L2, L1, F2, F1}), .clk(Clock_out), .clr(Clear));
  Clock Clock (.out(Clock_out));
  LED Valid (.in(priority_encoder_5_out[0]));
endmodule
