// Logisim project markVII.circ as structural Verilog: 1 circuit, main circuit main
module main (
  input  Fan_1_On_Off,
  input  A2,
  input  A1,
  input  A0,
  input  Fan_2_On_Off,
  input  B2,
  input  B1,
  input  B0,
  input  Both_On__A,
  input  Light_2_On__B,
  input  Light_1_On__C,
  input  Both_Off__D,
  output F1,
  output F2,
  output L1,
  output L2
);

  wire adder_1_cout, adder_1_out, adder_2_cout, adder_2_out, Clear_out, Clock_out, nand_1_out, nand_2_out,
       nand_3_out, nand_4_out, nand_5_out, nand_6_out, nand_7_out, nand_8_out, nand_9_out,
       priority_encoder_1_en_out, priority_encoder_1_gs, priority_encoder_2_en_out, priority_encoder_2_gs,
       priority_encoder_3_en_out, priority_encoder_3_gs, priority_encoder_4_gs;
  wire [1:0] priority_encoder_1_out, priority_encoder_2_out, priority_encoder_3_out, priority_encoder_4_out;

  // Probe on priority_encoder_1_en_out
  Priority_Encoder #(.select(2)) priority_encoder_1 (
    .in0(A2), .in1(A1), .in2(A0), .in3(1'b0), .out(priority_encoder_1_out), .gs(priority_encoder_1_gs),
    .en_out(priority_encoder_1_en_out), .en_in(1'b1));
  // Probe on priority_encoder_2_en_out
  Priority_Encoder #(.select(2)) priority_encoder_2 (
    .in0(B2), .in1(B1), .in2(B0), .in3(1'b0), .out(priority_encoder_2_out), .gs(priority_encoder_2_gs),
    .en_out(priority_encoder_2_en_out), .en_in(1'b1));
  nand nand_1 (nand_1_out, Both_On__A, Both_On__A);
  nand nand_2 (nand_2_out, Light_2_On__B, Light_2_On__B);
  nand nand_3 (nand_3_out, Light_1_On__C, Light_1_On__C);
  nand nand_4 (nand_4_out, Both_Off__D, Both_Off__D);
  // Probe on priority_encoder_1_out
  // Probe on priority_encoder_2_out
  // Probe on priority_encoder_3_en_out
  // Probe on priority_encoder_3_gs
  Priority_Encoder #(.select(2), .disabled(0)) priority_encoder_3 (
    .in0(Both_Off__D), .in1(Light_1_On__C), .in2(Light_2_On__B), .in3(Both_On__A),
    .out(priority_encoder_3_out), .gs(priority_encoder_3_gs), .en_out(priority_encoder_3_en_out), .en_in(1'b1));
  Adder #(.width(1)) adder_1 (.a(nand_1_out), .b(nand_2_out), .out(adder_1_out), .cout(adder_1_cout));  // open: cin
  Adder #(.width(1)) adder_2 (.a(nand_3_out), .b(nand_4_out), .out(adder_2_out), .cout(adder_2_cout));  // open: cin
  // Probe on priority_encoder_4_out
  Priority_Encoder #(.select(2)) priority_encoder_4 (
    .in0(1'b0), .in1(priority_encoder_1_gs), .in2(priority_encoder_2_gs), .in3(nand_9_out),
    .out(priority_encoder_4_out), .gs(priority_encoder_4_gs), .en_in(1'b1));  // open: en_out
  nand nand_5 (nand_5_out, adder_1_out, adder_2_cout);
  nand nand_6 (nand_6_out, adder_1_cout, adder_2_out);
  nand nand_7 (nand_7_out, priority_encoder_4_gs, priority_encoder_4_gs);
  nand nand_8 (nand_8_out, nand_5_out, nand_6_out);
  nand nand_9 (nand_9_out, nand_8_out, nand_8_out);
  Register #(.width(4)) register_1 (
    .D({priority_encoder_3_out, Fan_2_On_Off, Fan_1_On_Off}), .en(nand_7_out), .Q({L2, L1, F2, F1}),
    .clk(Clock_out), .clr(Clear_out));
  Clock Clear (.out(Clear_out));
  Clock Clock (.out(Clock_out));
  LED Valid (.in(nand_7_out));

  // Notes on the sheet:
  //   B2+B1+B0+0
  //   (A'B'(C xor D) + C'D'(A xor B))'
  //   Enable/Valid: (A2+A1+A0+0 + B2+B1+B0+0 + (A'B'(C xor D) + C'D'(A xor B))')'
  //   F1
  //   BCD1
  //   0
  //   0000
  //   1
  //   1000
  //   0xxx
  //   Memory
  //   1xxx
  //   BCD3
  //   0001
  //   0010
  //   0100
  //   1000
  //   Anything else
  //   F2
  //   BCD2
  //   0
  //   0000
  //   1000
  //   1
  //   0xxx
  //   Memory
  //   1xxx
  //   L2
  //   L1
  //   0
  //   0
  //   1
  //   0
  //   0
  //   1
  //   1
  //   1
  //   Memory
endmodule
