// Logisim project markVIII.circ as structural Verilog: 1 circuit, main circuit main
module main (
  input  in_1,
  input  in_2,
  input  in_3,
  input  in_4,
  input  in_5,
  input  in_6,
  input  in_7,
  input  in_8,
  input  in_9,
  input  in_10,
  input  in_11,
  input  in_12,
  output F1,
  output F2,
  output L1,
  output L2
);

  wire and_1_out, and_2_out, clock_1_out, multiplexer_1_out, nand_1_out, nand_2_out, nand_3_out, nand_4_out,
       nand_5_out, not_1_out, not_2_out, priority_encoder_2_p4, shift_register_2_q0, shift_register_2_q1,
       shift_register_2_q2, shift_register_2_q3;
  wire [1:0] priority_encoder_1_out;
  wire [2:0] shift_register_1_out;
  wire [3:0] counter_1_q, shift_register_3_q3;

  Clock clock_1 (.out(clock_1_out));
  Counter #(.width(4), .max('hf)) counter_1 (
    .Q(counter_1_q), .clk(clock_1_out), .clr(and_1_out));  // open: load, D, count, carry
  nand nand_1 (nand_1_out, counter_1_q[2], counter_1_q[2]);
  Shift_Register #(.width(3), .length(4)) shift_register_1 (
    .shift(counter_1_q[2]), .clk(clock_1_out), .out(shift_register_1_out), .load(nand_1_out),
    .clr(and_2_out), .d0({in_1, in_2, in_3}), .d1({in_4, in_5, in_6}), .d2({in_7, in_8, in_9}),
    .d3({in_10, in_11, in_12}));  // open: in, q0, q1, q2, q3
  not not_1 (not_1_out, counter_1_q[2]);
  and and_1 (and_1_out, counter_1_q[3], counter_1_q[0], not_1_out, counter_1_q[1]);
  not not_2 (not_2_out, counter_1_q[0]);
  and and_2 (and_2_out, not_2_out, counter_1_q[1], not_1_out, counter_1_q[3]);
  Priority_Encoder #(.select(2)) priority_encoder_1 (
    .in0(shift_register_1_out[0]), .in1(shift_register_1_out[1]), .in2(shift_register_1_out[2]), .in3(1'b0),
    .out(priority_encoder_1_out));  // open: gs, en_out, en_in
  nand nand_2 (nand_2_out, shift_register_1_out[0], shift_register_1_out[0]);
  Shift_Register #(.length(4)) shift_register_2 (
    .shift(counter_1_q[2]), .in(multiplexer_1_out), .clk(clock_1_out), .clr(and_1_out),
    .q0(shift_register_2_q0), .q1(shift_register_2_q1), .q2(shift_register_2_q2), .q3(shift_register_2_q3));  // open: out, load, d0, d1, d2, d3
  // Priority_Encoder #(.select(2)) priority_encoder_2: pin names not known; wires that end beside it: shift_register_2_q0, shift_register_2_q1, shift_register_2_q2, priority_encoder_2_p4, shift_register_2_q3
  Multiplexer #(.select(2), .enable("false")) multiplexer_1 (
    .in0(nand_2_out), .in1(shift_register_1_out[0]), .in2(1'b1), .in3(1'b1), .out(multiplexer_1_out),
    .sel(shift_register_1_out[2:1]));
  nand nand_3 (nand_3_out, priority_encoder_2_p4, priority_encoder_2_p4);
  Shift_Register #(.length(4)) shift_register_3 (
    .shift(counter_1_q[2]), .in(priority_encoder_1_out[0]), .clk(clock_1_out), .q0(shift_register_3_q3[3]),
    .q1(shift_register_3_q3[2]), .q2(shift_register_3_q3[1]), .q3(shift_register_3_q3[0]));  // open: out, load, clr, d0, d1, d2, d3
  nand nand_4 (nand_4_out, nand_3_out, and_2_out);
  Register #(.width(4)) register_1 (
    .D(shift_register_3_q3), .en(nand_5_out), .Q({L2, L1, F2, F1}), .clk(clock_1_out));  // open: clr
  nand nand_5 (nand_5_out, nand_4_out, nand_4_out);
endmodule
