// Logisim project markX.circ as structural Verilog: 1 circuit, main circuit main
module main (
  input  A3,
  input  A2,
  input  A1,
  input  A0,
  input  B3,
  input  B2,
  input  B1,
  input  B0,
  input  C3,
  input  C2,
  input  C1,
  input  C0,
  output F1,
  output F2,
  output L1,
  output L2
);

  wire clock_1_out, decoder_1_out0, decoder_1_out1, decoder_1_out2, decoder_1_out3, decoder_1_out4,
       decoder_1_out5, decoder_1_out6, multiplexer_1_out, nand_1_out, nand_2_out, nand_3_out, nand_4_out,
       priority_encoder_1_gs, priority_encoder_3_p4, shift_register_2_q0, shift_register_2_q1,
       shift_register_2_q2, shift_register_2_q3;
  wire [1:0] priority_encoder_2_out;
  wire [2:0] counter_1_q, shift_register_1_out;
  wire [3:0] shift_register_3_q3;

  Clock clock_1 (.out(clock_1_out));
  Decoder #(.select(3), .enable("false")) decoder_1 (
    .out0(decoder_1_out0), .out1(decoder_1_out1), .out2(decoder_1_out2), .out3(decoder_1_out3),
    .out4(decoder_1_out4), .out5(decoder_1_out5), .out6(decoder_1_out6), .sel(counter_1_q));  // open: out7
  Counter #(.width(3), .max('h7)) counter_1 (
    .Q(counter_1_q), .clk(clock_1_out), .clr(decoder_1_out6));  // open: load, D, count, carry
  Priority_Encoder #(.select(2)) priority_encoder_1 (
    .in0(decoder_1_out1), .in1(decoder_1_out2), .in2(decoder_1_out3), .in3(decoder_1_out4),
    .gs(priority_encoder_1_gs));  // open: out, en_out, en_in
  Shift_Register #(.width(3), .length(4)) shift_register_1 (
    .shift(priority_encoder_1_gs), .in(shift_register_1_out), .clk(clock_1_out), .out(shift_register_1_out),
    .load(decoder_1_out0), .d0({A3, A2, A1}), .d1({A0, B3, B2}), .d2({B1, B0, C3}), .d3({C2, C1, C0}));  // open: clr, q0, q1, q2, q3
  Priority_Encoder #(.select(2)) priority_encoder_2 (
    .in0(shift_register_1_out[0]), .in1(shift_register_1_out[1]), .in2(shift_register_1_out[2]), .in3(1'b0),
    .out(priority_encoder_2_out));
  // Probe on priority_encoder_2_out[1]
  nand nand_1 (nand_1_out, shift_register_1_out[0], shift_register_1_out[0]);
  Shift_Register #(.length(4)) shift_register_2 (
    .shift(priority_encoder_1_gs), .in(multiplexer_1_out), .clk(clock_1_out), .q0(shift_register_2_q0),
    .q1(shift_register_2_q1), .q2(shift_register_2_q2), .q3(shift_register_2_q3));  // open: out, load, clr, d0, d1, d2, d3
  Multiplexer #(.select(2), .enable("false")) multiplexer_1 (
    .in0(nand_1_out), .in1(shift_register_1_out[0]), .in2(1'b1), .in3(1'b1), .out(multiplexer_1_out),
    .sel(shift_register_1_out[2:1]));
  // Priority_Encoder #(.select(2)) priority_encoder_3: pin names not known; wires that end beside it: shift_register_2_q0, shift_register_2_q1, shift_register_2_q2, priority_encoder_3_p4, shift_register_2_q3
  nand nand_2 (nand_2_out, priority_encoder_3_p4, priority_encoder_3_p4);
  Shift_Register #(.length(4)) shift_register_3 (
    .shift(priority_encoder_1_gs), .in(priority_encoder_2_out[0]), .clk(clock_1_out),
    .q0(shift_register_3_q3[3]), .q1(shift_register_3_q3[2]), .q2(shift_register_3_q3[1]),
    .q3(shift_register_3_q3[0]));  // open: out, load, clr, d0, d1, d2, d3
  nand nand_3 (nand_3_out, nand_2_out, decoder_1_out5);
  nand nand_4 (nand_4_out, nand_3_out, nand_3_out);
  Register #(.width(4)) register_1 (
    .D(shift_register_3_q3), .en(nand_4_out), .Q({L2, L1, F2, F1}), .clk(clock_1_out));  // open: clr
endmodule
