// Logisim project markXI.circ as structural Verilog: 1 circuit, main circuit main
module main (
  input  A3,
  input  A2,
  input  A1,
  input  A0,
  input  B3,
  input  B2,
  input  B1,
  input  B0,
  input  C3,
  input  C2,
  input  C1,
  input  C0,
  output F1,
  output F2,
  output L1,
  output L2
);

  wire and_1_out, clock_1_out, decoder_1_out0, decoder_1_out1, decoder_1_out2, decoder_1_out3,
       decoder_1_out4, decoder_1_out5, decoder_1_out6, decoder_2_out0, decoder_2_out1, decoder_2_out2,
       decoder_2_out3, decoder_2_out4, decoder_2_out5, decoder_2_out6, decoder_2_out7, not_1_out, or_1_out,
       or_2_out, priority_encoder_1_gs, priority_encoder_2_en_out, priority_encoder_2_out,
       priority_encoder_3_gs;
  wire [2:0] counter_1_q, shift_register_1_out;
  wire [3:0] shift_register_2_q3;

  Clock clock_1 (.out(clock_1_out));
  Decoder #(.select(3), .enable("false")) decoder_1 (
    .out0(decoder_1_out0), .out1(decoder_1_out1), .out2(decoder_1_out2), .out3(decoder_1_out3),
    .out4(decoder_1_out4), .out5(decoder_1_out5), .out6(decoder_1_out6), .sel(counter_1_q));  // open: out7
  Counter #(.width(3), .max('h7)) counter_1 (
    .Q(counter_1_q), .clk(clock_1_out), .clr(or_1_out));  // open: load, D, count, carry
  or or_1 (or_1_out, decoder_1_out6, or_2_out);
  Priority_Encoder #(.select(2)) priority_encoder_1 (
    .in0(decoder_1_out1), .in1(decoder_1_out2), .in2(decoder_1_out3), .in3(decoder_1_out4),
    .gs(priority_encoder_1_gs));  // open: out, en_out, en_in
  Shift_Register #(.width(3), .length(4)) shift_register_1 (
    .shift(priority_encoder_1_gs), .in(shift_register_1_out), .clk(clock_1_out), .out(shift_register_1_out),
    .load(decoder_1_out0), .d0({A3, A2, A1}), .d1({A0, B3, B2}), .d2({B1, B0, C3}), .d3({C2, C1, C0}));  // open: clr, q0, q1, q2, q3
  Decoder #(.select(3), .enable("false")) decoder_2 (
    .out0(decoder_2_out0), .out1(decoder_2_out1), .out2(decoder_2_out2), .out3(decoder_2_out3),
    .out4(decoder_2_out4), .out5(decoder_2_out5), .out6(decoder_2_out6), .out7(decoder_2_out7),
    .sel(shift_register_1_out));
  Priority_Encoder #(.select(1)) priority_encoder_2 (
    .in0(decoder_2_out1), .in1(decoder_2_out2), .out(priority_encoder_2_out),
    .en_out(priority_encoder_2_en_out));  // open: gs, en_in
  Priority_Encoder priority_encoder_3 (
    .in0(decoder_2_out0), .in1(decoder_2_out3), .in2(decoder_2_out4), .in3(decoder_2_out5),
    .in4(decoder_2_out6), .in5(decoder_2_out7), .in6(1'b0), .in7(1'b0), .gs(priority_encoder_3_gs));  // open: out, en_in, en_out
  or or_2 (or_2_out, priority_encoder_2_en_out, priority_encoder_3_gs);
  not not_1 (not_1_out, or_2_out);
  and and_1 (and_1_out, priority_encoder_1_gs, not_1_out);
  Shift_Register #(.length(4)) shift_register_2 (
    .shift(and_1_out), .in(priority_encoder_2_out), .clk(clock_1_out), .clr(or_2_out),
    .q0(shift_register_2_q3[3]), .q1(shift_register_2_q3[2]), .q2(shift_register_2_q3[1]),
    .q3(shift_register_2_q3[0]));  // open: out, load, d0, d1, d2, d3
  Register #(.width(4)) register_1 (
    .D(shift_register_2_q3), .en(decoder_1_out5), .Q({L2, L1, F2, F1}), .clk(clock_1_out));  // open: clr
  LED InValid (.in(or_2_out));
endmodule
